# Fritzing sketch project (saved by Fritzing 0.9.2b)
breadboards: 1

parts:
  Componente1 = Arduino Mega 2560 (Rev3)
  LED1 = LEDs [package=led10mm]  # not connected
  R1 = Resistor [tolerance=±5% resistance=330k package=THT]

nets:
  N1: Componente1.D52, R1.Pin_0, R1.Pin_1
